# Fritzing sketch CD4511B_1dig (saved by Fritzing 0.9.3b)
breadboards: 1

parts:
  DRIVERS1 = CD4511B
  Part2 = Arduino Board Ethernet
  7_Segment1 = 7 Segment Display
  R1 = Resistor [tolerance=±5% resistance=660 package="2010 [SMD]"]
  7_Segment2 = 7 Segment Display
  R2 = Resistor [tolerance=±5% resistance=660 package="2010 [SMD]"]
  7_Segment3 = 7 Segment Display
  R3 = Resistor [tolerance=±5% resistance=660 package="2010 [SMD]"]

nets:
  N1: DRIVERS1.B, Part2.D3_PWM
  N2: DRIVERS1.C, Part2.D4
  VCC: DRIVERS1.VCC1, DRIVERS1.VCC2, DRIVERS1.VCC, Part2.5V
  GND: DRIVERS1.GND1, DRIVERS1.GND, Part2.GND
  N3: DRIVERS1.D, Part2.D5_PWM
  N4: DRIVERS1.A, Part2.D2_PWM
  N5: DRIVERS1.e, 7_Segment1.Segment_E
  N6: DRIVERS1.d, 7_Segment1.Segment_D
  N7: DRIVERS1.c, 7_Segment1.Segment_C
  N8: DRIVERS1.b, 7_Segment3.Segment_B
  N9: DRIVERS1.a, 7_Segment3.Segment_A
  N10: DRIVERS1.g, 7_Segment3.Segment_F
  N11: DRIVERS1.f, 7_Segment3.Segment_G
  N12: Part2.D8, R3.Pin_1
  N13: Part2.D6_PWM, R1.Pin_1
  N14: Part2.D7, R2.Pin_1
  N15: 7_Segment1.common_anode, R1.Pin_0
  N16: 7_Segment2.common_anode, R2.Pin_0
  N17: 7_Segment3.common_anode, R3.Pin_0

custom parts:
  CD4511B: Finally....
