# Fritzing sketch Counter (saved by Fritzing 0.9.3b)
breadboards: 1

parts:
  Part1 = Arduino Uno (Rev3)
  S1 = Pushbutton [package="[THT]"]
  S2 = Pushbutton [package="[THT]"]
  S3 = Pushbutton [package="[THT]"]
  S4 = Pushbutton [package="[THT]"]
  7_Segment1 = 7 Segment Display
  7_Segment2 = 7 Segment Display
  7_Segment3 = 7 Segment Display
  DRIVERS1 = CD4511B
  R1 = Resistor [tolerance=±5% resistance=1k package="1206 [SMD]"]
  R2 = Resistor [tolerance=±5% resistance=1k package="1206 [SMD]"]
  R3 = Resistor [tolerance=±5% resistance=1k package="1206 [SMD]"]
  R4 = Resistor [tolerance=±5% resistance=1k package="1206 [SMD]"]

nets:
  N1: Part1.D8, 7_Segment2.common_anode
  N2: Part1.D9_PWM, DRIVERS1.A
  N3: Part1.D10_PWM/SS, DRIVERS1.B
  N4: Part1.D11_PWM/MOSI, DRIVERS1.C
  N5: Part1.D12/MISO, DRIVERS1.D
  N6: Part1.D2, S1.Pin_3, S1.Pin_4, R2.Pin_1
  N7: Part1.D3_PWM, S2.Pin_3, S2.Pin_4, R3.Pin_1
  N8: Part1.D4, S3.Pin_3, S3.Pin_4, R4.Pin_1
  N9: Part1.D5_PWM, S4.Pin_3, S4.Pin_4, R1.Pin_1
  N10: Part1.D6_PWM, 7_Segment3.common_anode
  N11: Part1.D7, 7_Segment1.common_anode
  5V: Part1.5V, S1.Pin_1, S1.Pin_2, S2.Pin_1, S2.Pin_2, S3.Pin_1, S3.Pin_2, S4.Pin_1, S4.Pin_2, DRIVERS1.VCC1, DRIVERS1.VCC2, DRIVERS1.VCC
  GND: Part1.GND, DRIVERS1.GND1, DRIVERS1.GND, R1.Pin_0, R2.Pin_0, R3.Pin_0, R4.Pin_0
  N12: 7_Segment3.Segment_E, DRIVERS1.e
  N13: 7_Segment3.Segment_D, DRIVERS1.d
  N14: 7_Segment3.Segment_C, DRIVERS1.c
  N15: 7_Segment3.Segment_B, DRIVERS1.b
  N16: 7_Segment3.Segment_A, DRIVERS1.a
  N17: 7_Segment3.Segment_F, DRIVERS1.f
  N18: 7_Segment3.Segment_G, DRIVERS1.g

custom parts:
  CD4511B: Finally....
