# Fritzing sketch Elevator (saved by Fritzing 0.9.3b)
breadboards: 1

parts:
  Part1 = Arduino Board Ethernet
  S1 = Pushbutton [package="[SMD]"]
  DRIVERS1 = CD4511B
  R1 = Resistor [tolerance=±5% resistance=1k package=THT]
  LED1 = smd LED [color="Red (633nm)" package="1206 [SMD]"]
  7_Segment1 = 7 Segment Display
  S2 = Pushbutton [package="[SMD]"]
  S3 = Pushbutton [package="[SMD]"]
  S4 = Pushbutton [package="[SMD]"]
  S5 = Pushbutton [package="[SMD]"]
  S6 = Pushbutton [package="[SMD]"]
  LED2 = smd LED [color="Red (633nm)" package="1206 [SMD]"]
  LED3 = smd LED [color="Red (633nm)" package="1206 [SMD]"]
  LED4 = smd LED [color="Red (633nm)" package="1206 [SMD]"]
  LED5 = smd LED [color="Red (633nm)" package="1206 [SMD]"]
  R2 = Resistor [tolerance=±5% resistance=1k package=THT]
  R3 = Resistor [tolerance=±5% resistance=1k package=THT]
  R4 = Resistor [tolerance=±5% resistance=1k package=THT]
  R5 = Resistor [tolerance=±5% resistance=1k package=THT]
  R6 = Resistor [tolerance=±5% resistance=1k package=THT]
  R7 = Resistor [tolerance=±5% resistance=660 package=THT]
  R8 = Resistor [tolerance=±5% resistance=660 package=THT]
  R9 = Resistor [tolerance=±5% resistance=660 package=THT]
  R10 = Resistor [tolerance=±5% resistance=660 package=THT]
  R11 = Resistor [tolerance=±5% resistance=660 package=THT]
  R12 = Resistor [tolerance=±5% resistance=660 package=THT]

nets:
  N1: Part1.D8, S3.Pin_3, S3.Pin_4, R4.Pin_1
  N2: Part1.D9_PWM, S4.Pin_3, S4.Pin_4, R5.Pin_1
  N3: Part1.D10_PWM/SS, S5.Pin_3, S5.Pin_4, R6.Pin_1
  N4: Part1.D11/MOSI, R1.Pin_1, S6.Pin_3, S6.Pin_4
  GND: Part1.GND, DRIVERS1.GND1, DRIVERS1.GND, R1.Pin_0, S6.Pin_1, S6.Pin_2, R2.Pin_0, R3.Pin_0, R4.Pin_0, R5.Pin_0, R6.Pin_0, R7.Pin_0, R8.Pin_0, R9.Pin_0, R10.Pin_0, R11.Pin_0, R12.Pin_0
  N5: Part1.A0, LED1.anode
  N6: Part1.A1, LED2.anode
  N7: Part1.A2, LED3.anode
  N8: Part1.A3, LED4.anode
  N9: Part1.A4, LED5.anode
  N10: Part1.D2_PWM, DRIVERS1.A
  N11: Part1.D3_PWM, DRIVERS1.B
  N12: Part1.D4, DRIVERS1.C
  N13: Part1.D5_PWM, DRIVERS1.D
  N14: Part1.D6_PWM, S1.Pin_3, S1.Pin_4, R2.Pin_1
  N15: Part1.D7, S2.Pin_3, S2.Pin_4, R3.Pin_1
  5V: Part1.5V, S1.Pin_1, S1.Pin_2, DRIVERS1.VCC1, DRIVERS1.VCC2, DRIVERS1.VCC, S2.Pin_1, S2.Pin_2, S3.Pin_1, S3.Pin_2, S4.Pin_1, S4.Pin_2, S5.Pin_1, S5.Pin_2
  N16: DRIVERS1.e, 7_Segment1.Segment_E
  N17: DRIVERS1.d, 7_Segment1.Segment_D
  N18: DRIVERS1.c, 7_Segment1.Segment_C
  N19: DRIVERS1.b, 7_Segment1.Segment_B
  N20: DRIVERS1.a, 7_Segment1.Segment_A
  N21: DRIVERS1.g, 7_Segment1.Segment_F
  N22: DRIVERS1.f, 7_Segment1.Segment_G
  N23: LED1.cathode, R12.Pin_1
  N24: 7_Segment1.common_anode, R7.Pin_1
  N25: LED2.cathode, R11.Pin_1
  N26: LED3.cathode, R8.Pin_1
  N27: LED4.cathode, R9.Pin_1
  N28: LED5.cathode, R10.Pin_1

custom parts:
  CD4511B: Finally....
